# Fritzing sketch Sensor CO2 y Temperatura (saved by Fritzing 0.9.3b)

parts:
  U1 = NodeMCU V1.0
  Mod1 = KY-015 Temperature & Humidity Sensor Module [package="Breakout board"]
  Mod2 = MQ-7 breakout

nets:
  N1: U1.D1, Mod1.S
  3V3: U1.3V3, Mod1.Vin
  GND: U1.GND, Mod1.-, Mod2.GND
  VIN: U1.Vin, Mod2.VCC
  N2: U1.A0, Mod2.AO

custom parts:
  NodeMCU V1.0: ESP8266 based NodeMCU
  KY-015 Temperature & Humidity Sensor Module: KY-015 temperature and humidity sensor module, provides a low-latency serial interface to measure humidity and temperature.
  MQ-7 breakout: MQ-5 gas sensor
